// Logisim project logicProject.circ as structural Verilog: 1 circuit, main circuit main
module main (
  input  [1:0] A,
  input  [1:0] B,
  input  As,
  input  Bs,
  output F0,
  output F1,
  output BI,
  output S
);

  wire and_1_out, and_2_out, comparator_1_eq, comparator_1_gt, comparator_1_lt, n7448_1_p10, n7448_1_p11,
       n7448_1_p12, n7448_1_p13, n7448_1_p14, n7448_1_p15, n7448_1_p16, xor_1_out, xor_2_out, xor_3_out;

  Comparator #(.width(2), .mode("unsigned")) comparator_1 (
    .a(A), .b(B), .gt(comparator_1_gt), .eq(comparator_1_eq), .lt(comparator_1_lt));
  or or_1 (BI, B[0], B[1]);
  xor xor_1 (xor_1_out, As, Bs);
  LED Fz (.in(comparator_1_lt));
  xor xor_2 (xor_2_out, 1'b1, BI);
  xor xor_3 (xor_3_out, comparator_1_lt, 1'b1);
  and and_1 (and_1_out, A[0], comparator_1_gt);
  LED F_z (.in(xor_2_out));
  and and_2 (and_2_out, xor_3_out, xor_1_out);
  and and_3 (S, and_2_out, BI);
  or or_2 (F0, comparator_1_eq, and_1_out);
  and and_4 (F1, comparator_1_gt, B[0]);
  // _7448 7448_1: pin names not known; wires that end beside it: F1, 1'b0, BI, 1'b1, 1'b1, 1'b0, F0, 1'b0, 1'b1, n7448_1_p10, n7448_1_p11, n7448_1_p12, n7448_1_p13, n7448_1_p14, n7448_1_p15, n7448_1_p16
  _7_Segment_Display u_7_segment_display_1 (.g(S));  // open: f, a, b, e, d, c, dp
  _7_Segment_Display u_7_segment_display_2 (
    .g(n7448_1_p11), .f(n7448_1_p10), .a(n7448_1_p12), .b(n7448_1_p13), .e(n7448_1_p16), .d(n7448_1_p15),
    .c(n7448_1_p14));  // open: dp

  // Notes on the sheet:
  //   A
  //   B
  //   Note1: the seven segment doesn't turn off, it gives 8 instead, when you apply LOW on BL pin (library problem)
endmodule
